// Logisim project Adding and subratcing.circ as structural Verilog: 8 circuits, main circuit Addition and subratction
module Addition_and_subratction (
  input  [4:0] A,
  input  [4:0] in_2,
  input  [1:0] in_3,
  output [7:0] Result,
  output Sign
);

  wire comparator_1_eq, not_1_out;
  wire [3:0] multiplexer_1_out, multiplexer_2_out, n2_s_complement_1_out_2, n2_s_complement_2_out_2;
  wire [4:0] n2_s_complemet_5_bits_1_out_2, n6bit_6bit_1_out_3;
  wire [5:5] multiplexer_3_out;

  _2_s_complement u_2_s_complement_1 (.in_1(A[3:0]), .out_2(n2_s_complement_1_out_2));
  _2_s_complement u_2_s_complement_2 (.in_1(in_2[3:0]), .out_2(n2_s_complement_2_out_2));
  Comparator #(.width(2), .mode("unsigned")) comparator_1 (.a(in_3), .b(2'b01), .eq(comparator_1_eq));  // open: gt, lt
  Multiplexer #(.width(4)) multiplexer_1 (
    .in0(A[3:0]), .in1(n2_s_complement_1_out_2), .out(multiplexer_1_out), .sel(A[4]));  // open: en
  Multiplexer #(.width(4)) multiplexer_2 (
    .in0(in_2[3:0]), .in1(n2_s_complement_2_out_2), .out(multiplexer_2_out), .sel(multiplexer_3_out[5]));  // open: en
  not not_1 (not_1_out, in_2[4]);
  Multiplexer multiplexer_3 (
    .in0(in_2[4]), .in1(not_1_out), .out(multiplexer_3_out[5]), .sel(comparator_1_eq));  // open: en
  _6bit_6bit u_6bit_6bit_1 (
    .in_1({{2{A[4]}}, multiplexer_1_out}), .in_2({{2{multiplexer_3_out[5]}}, multiplexer_2_out}),
    .out_3(n6bit_6bit_1_out_3), .Sign(Sign));
  _2_s_complemet_5_bits u_2_s_complemet_5_bits_1 (.in_1(n6bit_6bit_1_out_3), .out_2(n2_s_complemet_5_bits_1_out_2));
  Multiplexer #(.width(5)) multiplexer_4 (
    .in0(n6bit_6bit_1_out_3), .in1(n2_s_complemet_5_bits_1_out_2), .out(Result[4:0]), .sel(Sign));  // open: en

  assign Result[7:5] = 3'b000;

  // Notes on the sheet:
  //   B
  //   2's complemet of  4 bits
  //   2's complement of 4 bits
  //   2's complement of 5 bits
endmodule

module _2_s_complement (
  input  [3:0] in_1,
  output [3:0] out_2
);

  wire comparator_1_eq;
  wire [3:0] n1_bit_4_bits_1_out_2, not_1_out;

  Comparator #(.width(4), .mode("unsigned")) comparator_1 (
    .a(in_1), .b(4'b0000), .eq(comparator_1_eq));  // open: gt, lt
  assign not_1_out = ~in_1;  // NOT_Gate not_1, 4 bits wide
  _1_bit_4_bits u_1_bit_4_bits_1 (.in_1(not_1_out), .out_2(n1_bit_4_bits_1_out_2));
  Multiplexer #(.width(4)) multiplexer_1 (
    .in0(n1_bit_4_bits_1_out_2), .in1(in_1), .out(out_2), .sel(comparator_1_eq));  // open: en
endmodule

module _1_bit_4_bits (
  input  [3:0] in_1,
  output [3:0] out_2
);

  wire half_adder_1_carry, half_adder_2_carry, half_adder_3_carry, half_adder_4_carry;

  half_adder half_adder_1 (.in_1(in_1[0]), .in_2(1'b1), .sum(out_2[0]), .carry(half_adder_1_carry));
  half_adder half_adder_2 (.in_1(half_adder_1_carry), .in_2(in_1[1]), .sum(out_2[1]), .carry(half_adder_2_carry));
  half_adder half_adder_3 (.in_1(half_adder_2_carry), .in_2(in_1[2]), .sum(out_2[2]), .carry(half_adder_3_carry));
  half_adder half_adder_4 (.in_1(half_adder_3_carry), .in_2(in_1[3]), .sum(out_2[3]), .carry(half_adder_4_carry));
  // also tied to GND on the sheet: half_adder_4_carry

  // Notes on the sheet:
  //   HA
  //   HA
  //   HA
  //   HA
endmodule

module _6bit_6bit (
  input  [5:0] in_1,
  input  [5:0] in_2,
  output [4:0] out_3,
  output Sign
);

  wire full_aider_1_carry, full_aider_2_carry, full_aider_3_carry, full_aider_4_carry, full_aider_5_carry,
       half_adder_1_carry;

  half_adder half_adder_1 (.in_1(in_1[0]), .in_2(in_2[0]), .sum(out_3[0]), .carry(half_adder_1_carry));
  Full_Aider full_aider_1 (
    .a(in_1[1]), .b(in_2[1]), .c(half_adder_1_carry), .sum(out_3[1]), .carry(full_aider_1_carry));
  Full_Aider full_aider_2 (
    .a(in_1[2]), .b(in_2[2]), .c(full_aider_1_carry), .sum(out_3[2]), .carry(full_aider_2_carry));
  Full_Aider full_aider_3 (
    .a(in_1[3]), .b(in_2[3]), .c(full_aider_2_carry), .sum(out_3[3]), .carry(full_aider_3_carry));
  Full_Aider full_aider_4 (
    .a(in_1[4]), .b(in_2[4]), .c(full_aider_3_carry), .sum(out_3[4]), .carry(full_aider_4_carry));
  Full_Aider full_aider_5 (.a(in_1[5]), .b(in_2[5]), .c(full_aider_4_carry), .sum(Sign), .carry(full_aider_5_carry));
  // also tied to GND on the sheet: full_aider_5_carry

  // Notes on the sheet:
  //   HA
  //   FA
  //   FA
  //   FA
  //   FA
  //   FA
endmodule

module Full_Aider (
  input  a,
  input  b,
  input  c,
  output sum,
  output carry
);

  wire half_adder_1_carry, half_adder_1_sum, half_adder_2_carry;

  half_adder half_adder_1 (.in_1(a), .in_2(b), .sum(half_adder_1_sum), .carry(half_adder_1_carry));
  half_adder half_adder_2 (.in_1(half_adder_1_sum), .in_2(c), .sum(sum), .carry(half_adder_2_carry));
  or or_1 (carry, half_adder_2_carry, half_adder_1_carry);
endmodule

module _2_s_complemet_5_bits (
  input  [4:0] in_1,
  output [4:0] out_2
);

  wire comparator_1_eq;
  wire [4:0] n1bit_5_bits_1_out_2, not_1_out;

  Comparator #(.width(5), .mode("unsigned")) comparator_1 (
    .a(in_1), .b({5{1'b0}}), .eq(comparator_1_eq));  // open: gt, lt
  assign not_1_out = ~in_1;  // NOT_Gate not_1, 5 bits wide
  _1bit_5_bits u_1bit_5_bits_1 (.in_1(not_1_out), .out_2(n1bit_5_bits_1_out_2));
  Multiplexer #(.width(5)) multiplexer_1 (
    .in0(n1bit_5_bits_1_out_2), .in1(in_1), .out(out_2), .sel(comparator_1_eq));  // open: en
endmodule

module _1bit_5_bits (
  input  [4:0] in_1,
  output [4:0] out_2
);

  wire half_adder_1_carry, half_adder_2_carry, half_adder_3_carry, half_adder_4_carry, half_adder_5_carry;

  half_adder half_adder_1 (.in_1(in_1[0]), .in_2(1'b1), .sum(out_2[0]), .carry(half_adder_1_carry));
  half_adder half_adder_2 (.in_1(half_adder_1_carry), .in_2(in_1[1]), .sum(out_2[1]), .carry(half_adder_2_carry));
  half_adder half_adder_3 (.in_1(half_adder_2_carry), .in_2(in_1[2]), .sum(out_2[2]), .carry(half_adder_3_carry));
  half_adder half_adder_4 (.in_1(half_adder_3_carry), .in_2(in_1[3]), .sum(out_2[3]), .carry(half_adder_4_carry));
  half_adder half_adder_5 (.in_1(in_1[4]), .in_2(half_adder_4_carry), .sum(out_2[4]), .carry(half_adder_5_carry));
  // also tied to GND on the sheet: half_adder_5_carry
endmodule

module half_adder (
  input  in_1,
  input  in_2,
  output sum,
  output carry
);

  xor xor_1 (sum, in_1, in_2);
  and and_1 (carry, in_1, in_2);
endmodule
