// Logisim project BinaryToBCDFinal.circ as structural Verilog: 2 circuits, main circuit ADD3-Module
module ADD3_Module (
  input  A0,
  input  A1,
  input  A2,
  input  A3,
  output out_5,
  output out_6,
  output out_7,
  output out_8
);

  wire and_1_out, and_2_out, and_3_out, and_4_out, and_5_out, and_6_out, and_7_out, and_8_out, and_9_out,
       and_10_out, and_11_out, and_12_out, and_13_out, and_14_out, and_15_out, and_16_out, not_1_out,
       not_2_out, not_3_out, not_4_out, or_1_out, or_2_out, or_5_out;

  not not_1 (not_1_out, A1);
  not not_2 (not_2_out, A0);
  not not_3 (not_3_out, A3);
  not not_4 (not_4_out, A2);
  and and_1 (and_1_out, A2, A1);
  and and_2 (and_2_out, A2, A0);
  and and_3 (and_3_out, A3, not_1_out);
  and and_4 (and_4_out, A2, A1);
  and and_5 (and_5_out, not_4_out, not_3_out);
  and and_6 (and_6_out, A1, A0);
  and and_7 (and_7_out, A3, A0);
  and and_8 (and_8_out, and_3_out, not_2_out);
  and and_9 (and_9_out, and_4_out, not_2_out);
  and and_10 (and_10_out, and_5_out, A0);
  and and_11 (and_11_out, not_3_out, not_4_out);
  and and_12 (and_12_out, A3, not_1_out);
  and and_13 (and_13_out, A2, not_1_out);
  or or_1 (or_1_out, A3, and_1_out);
  or or_2 (or_2_out, and_8_out, and_9_out);
  and and_14 (and_14_out, and_11_out, A1);
  and and_15 (and_15_out, and_13_out, not_2_out);
  or or_3 (out_8, or_1_out, and_2_out);
  or or_4 (out_5, or_2_out, and_10_out);
  and and_16 (and_16_out, and_12_out, not_2_out);
  or or_5 (or_5_out, and_14_out, and_6_out);
  or or_6 (out_7, and_15_out, and_7_out);
  or or_7 (out_6, or_5_out, and_16_out);
endmodule

module Binary_to_BCD_Converter (
  input  B0,
  input  B1,
  input  B2,
  input  B3,
  input  B4,
  input  B5,
  input  B6,
  input  B7,
  output UNITS,
  output out_10,
  output out_11,
  output out_12,
  output TENTH,
  output out_14,
  output out_15,
  output out_16,
  output HUND,
  output out_18,
  output out_19,
  output out_20
);

  wire add3_module_1_out_5, add3_module_1_out_6, add3_module_1_out_7, add3_module_1_out_8,
       add3_module_2_out_5, add3_module_2_out_6, add3_module_2_out_7, add3_module_2_out_8,
       add3_module_3_out_5, add3_module_3_out_6, add3_module_3_out_7, add3_module_3_out_8,
       add3_module_4_out_5, add3_module_4_out_6, add3_module_4_out_7, c1_out_5, c1_out_6, c1_out_7, c1_out_8;

  ADD3_Module c1 (
    .A0(B5), .A1(B6), .A2(B7), .A3(1'b0), .out_5(c1_out_5), .out_6(c1_out_6), .out_7(c1_out_7),
    .out_8(c1_out_8));
  ADD3_Module add3_module_1 (
    .A0(B4), .A1(c1_out_5), .A2(c1_out_6), .A3(c1_out_7), .out_5(add3_module_1_out_5),
    .out_6(add3_module_1_out_6), .out_7(add3_module_1_out_7), .out_8(add3_module_1_out_8));
  ADD3_Module add3_module_2 (
    .A0(B3), .A1(add3_module_1_out_5), .A2(add3_module_1_out_6), .A3(add3_module_1_out_7),
    .out_5(add3_module_2_out_5), .out_6(add3_module_2_out_6), .out_7(add3_module_2_out_7),
    .out_8(add3_module_2_out_8));
  ADD3_Module add3_module_3 (
    .A0(B2), .A1(add3_module_2_out_5), .A2(add3_module_2_out_6), .A3(add3_module_2_out_7),
    .out_5(add3_module_3_out_5), .out_6(add3_module_3_out_6), .out_7(add3_module_3_out_7),
    .out_8(add3_module_3_out_8));
  ADD3_Module add3_module_4 (
    .A0(add3_module_2_out_8), .A1(add3_module_1_out_8), .A2(c1_out_8), .A3(1'b0),
    .out_5(add3_module_4_out_5), .out_6(add3_module_4_out_6), .out_7(add3_module_4_out_7), .out_8(out_18));
  ADD3_Module add3_module_5 (
    .A0(B1), .A1(add3_module_3_out_5), .A2(add3_module_3_out_6), .A3(add3_module_3_out_7), .out_5(out_10),
    .out_6(out_11), .out_7(out_12), .out_8(TENTH));
  ADD3_Module add3_module_6 (
    .A0(add3_module_3_out_8), .A1(add3_module_4_out_5), .A2(add3_module_4_out_6), .A3(add3_module_4_out_7),
    .out_5(out_14), .out_6(out_15), .out_7(out_16), .out_8(HUND));

  assign out_19 = 1'b0;
  assign out_20 = 1'b0;
  assign UNITS = B0;

  // Notes on the sheet:
  //   add3-module
  //   add3-module
  //   c2
  //   add3-mod
  //   c3
  //   add3-module
  //   c4
  //   c6
  //   add3-module
  //   c5
  //   add3-mod
  //   c7
  //   add3-module
endmodule
