// Logisim project Division-FINAL-41.circ as structural Verilog
module Full_Subtractor (
  input  [3:0] in_1,
  input  [3:0] in_2,
  output [3:0] out_3
);

  Half_Subtractor half_subtractor_1 (.in_1(in_1[3]), .in_2(in_2[3]), .out_3(out_3[3]));
  Half_Subtractor half_subtractor_2 (.in_1(in_1[2]), .in_2(in_2[2]), .out_3(out_3[2]));
  Half_Subtractor half_subtractor_3 (.in_1(in_1[1]), .in_2(in_2[1]), .out_3(out_3[1]));
  Half_Subtractor half_subtractor_4 (.in_1(in_1[0]), .in_2(in_2[0]), .out_3(out_3[0]));
endmodule

module Division (
  input  [4:0] in_1,
  input  [4:0] in_2,
  output Sign,
  output [7:0] out_4
);

  wire comparator_1_lt, comparator_2_lt, comparator_3_lt, comparator_4_lt;
  wire [3:0] full_subtractor_1_out_3, full_subtractor_2_out_3, full_subtractor_3_out_3, main_1_out_3,
       main_2_out_3, main_3_out_3;

  xor xor_1 (Sign, in_2[4], in_1[4]);
  Comparator #(.width(4), .mode("unsigned")) comparator_1 (
    .a({3'b000, in_1[3]}), .b(in_2[3:0]), .lt(comparator_1_lt));  // open: gt, eq
  not not_1 (out_4[3], comparator_1_lt);
  bit_by_bit_Multiplication_main main_1 (.in_1(in_2[3:0]), .in_2(out_4[3]), .out_3(main_1_out_3));
  Full_Subtractor full_subtractor_1 (.in_1({3'b000, in_1[3]}), .in_2(main_1_out_3), .out_3(full_subtractor_1_out_3));
  Comparator #(.width(4), .mode("unsigned")) comparator_2 (
    .a({full_subtractor_1_out_3[2:0], in_1[2]}), .b(in_2[3:0]), .lt(comparator_2_lt));  // open: gt, eq
  bit_by_bit_Multiplication_main main_2 (.in_1(in_2[3:0]), .in_2(out_4[2]), .out_3(main_2_out_3));
  not not_2 (out_4[2], comparator_2_lt);
  Full_Subtractor full_subtractor_2 (
    .in_1({full_subtractor_1_out_3[2:0], in_1[2]}), .in_2(main_2_out_3), .out_3(full_subtractor_2_out_3));
  Comparator #(.width(4), .mode("unsigned")) comparator_3 (
    .a({full_subtractor_2_out_3[2:0], in_1[1]}), .b(in_2[3:0]), .lt(comparator_3_lt));  // open: gt, eq
  not not_3 (out_4[1], comparator_3_lt);
  bit_by_bit_Multiplication_main main_3 (.in_1(in_2[3:0]), .in_2(out_4[1]), .out_3(main_3_out_3));
  Full_Subtractor full_subtractor_3 (
    .in_1({full_subtractor_2_out_3[2:0], in_1[1]}), .in_2(main_3_out_3), .out_3(full_subtractor_3_out_3));
  Comparator #(.width(4), .mode("unsigned")) comparator_4 (
    .a({full_subtractor_3_out_3[2:0], in_1[0]}), .b(in_2[3:0]), .lt(comparator_4_lt));  // open: gt, eq
  not not_4 (out_4[0], comparator_4_lt);

  assign out_4[7:4] = 4'b0000;
endmodule

module Half_Subtractor (
  input  in_1,
  input  in_2,
  output out_3
);

  xor xor_1 (out_3, in_1, in_2);
endmodule
