// Logisim project Main Project of Logic.circ as structural Verilog: 2 circuits, main circuit main
module main (
  input  [1:0] in_1,
  input  [4:0] in_2,
  input  [4:0] B,
  output Div_by_Zero,
  output Sign,
  output out_6
);

  wire binary_to_bcd_converter_1_hund, binary_to_bcd_converter_1_out_10, binary_to_bcd_converter_1_out_11,
       binary_to_bcd_converter_1_out_12, binary_to_bcd_converter_1_out_14, binary_to_bcd_converter_1_out_15,
       binary_to_bcd_converter_1_out_16, binary_to_bcd_converter_1_out_18, binary_to_bcd_converter_1_out_19,
       binary_to_bcd_converter_1_out_20, binary_to_bcd_converter_1_tenth, binary_to_bcd_converter_1_units,
       main_1_a, main_1_b, main_1_c, main_1_d, main_1_e, main_1_f, main_1_g, main_2_a, main_2_b, main_2_c,
       main_2_d, main_2_e, main_2_f, main_2_g, main_3_a, main_3_b, main_3_c, main_3_d, main_3_e, main_3_f,
       main_3_g;
  wire [7:0] ALU_result;

  ALU ALU (
    .A(in_2), .B(B), .in_1(in_1), .Sign_Flag(Sign), .Zero_Flag(out_6), .Div_by_Zero_Flag(Div_by_Zero),
    .Result(ALU_result));
  Binary_to_BCD_Converter binary_to_bcd_converter_1 (
    .B0(ALU_result[0]), .B1(ALU_result[1]), .B2(ALU_result[2]), .B3(ALU_result[3]), .B4(ALU_result[4]),
    .B5(ALU_result[5]), .B6(ALU_result[6]), .B7(ALU_result[7]), .UNITS(binary_to_bcd_converter_1_units),
    .out_10(binary_to_bcd_converter_1_out_10), .out_11(binary_to_bcd_converter_1_out_11),
    .out_12(binary_to_bcd_converter_1_out_12), .TENTH(binary_to_bcd_converter_1_tenth),
    .out_14(binary_to_bcd_converter_1_out_14), .out_15(binary_to_bcd_converter_1_out_15),
    .out_16(binary_to_bcd_converter_1_out_16), .HUND(binary_to_bcd_converter_1_hund),
    .out_18(binary_to_bcd_converter_1_out_18), .out_19(binary_to_bcd_converter_1_out_19),
    .out_20(binary_to_bcd_converter_1_out_20));
  Seven_Segment_FINALONE_main main_1 (
    .A0(binary_to_bcd_converter_1_units), .A1(binary_to_bcd_converter_1_out_10),
    .A2(binary_to_bcd_converter_1_out_11), .A3(binary_to_bcd_converter_1_out_12), .a(main_1_a), .b(main_1_b),
    .c(main_1_c), .d(main_1_d), .e(main_1_e), .f(main_1_f), .g(main_1_g));
  Seven_Segment_FINALONE_main main_2 (
    .A0(binary_to_bcd_converter_1_tenth), .A1(binary_to_bcd_converter_1_out_14),
    .A2(binary_to_bcd_converter_1_out_15), .A3(binary_to_bcd_converter_1_out_16), .a(main_2_a), .b(main_2_b),
    .c(main_2_c), .d(main_2_d), .e(main_2_e), .f(main_2_f), .g(main_2_g));
  Seven_Segment_FINALONE_main main_3 (
    .A0(binary_to_bcd_converter_1_hund), .A1(binary_to_bcd_converter_1_out_18),
    .A2(binary_to_bcd_converter_1_out_19), .A3(binary_to_bcd_converter_1_out_20), .a(main_3_a), .b(main_3_b),
    .c(main_3_c), .d(main_3_d), .e(main_3_e), .f(main_3_f), .g(main_3_g));
  _7_Segment_Display u_7_segment_display_1 (
    .g(main_1_g), .f(main_1_f), .a(main_1_a), .b(main_1_b), .e(main_1_e), .d(main_1_d), .c(main_1_c),
    .dp(1'b0));
  _7_Segment_Display u_7_segment_display_2 (
    .g(main_2_g), .f(main_2_f), .a(main_2_a), .b(main_2_b), .e(main_2_e), .d(main_2_d), .c(main_2_c),
    .dp(1'b0));
  _7_Segment_Display u_7_segment_display_3 (
    .g(main_3_g), .f(main_3_f), .a(main_3_a), .b(main_3_b), .e(main_3_e), .d(main_3_d), .c(main_3_c),
    .dp(1'b0));

  // Notes on the sheet:
  //   A
  //   Methods of operation
  //   Zero Flag
  //   Binary To BCD conversion
  //   BCD to 7 Segment
  //   Units
  //   Tens
  //   Hundreds
endmodule

module ALU (
  input  [1:0] in_1,
  input  [4:0] A,
  input  [4:0] B,
  output [7:0] Result,
  output Div_by_Zero_Flag,
  output Zero_Flag,
  output Sign_Flag
);

  wire addition_and_subratction_1_sign, comparator_1_eq, comparator_2_eq, division_1_sign,
       multiplication_1_f9;
  wire [7:0] addition_and_subratction_1_result, division_1_out_4, multiplexer_3_out, multiplication_1_f1;

  Addition_and_subratction addition_and_subratction_1 (
    .A(A), .in_2(B), .in_3(in_1), .Result(addition_and_subratction_1_result),
    .Sign(addition_and_subratction_1_sign));
  Division division_1 (.in_1(A), .in_2(B), .Sign(division_1_sign), .out_4(division_1_out_4));
  multiplication multiplication_1 (
    .a0(A[0]), .a1(A[1]), .a2(A[2]), .a3(A[3]), .a4(A[4]), .b0(B[0]), .b1(B[1]), .b2(B[2]), .b3(B[3]),
    .b4(B[4]), .f1(multiplication_1_f1[0]), .f2(multiplication_1_f1[1]), .f3(multiplication_1_f1[2]),
    .f4(multiplication_1_f1[3]), .f5(multiplication_1_f1[4]), .f6(multiplication_1_f1[5]),
    .f7(multiplication_1_f1[6]), .f8(multiplication_1_f1[7]), .f9(multiplication_1_f9));
  Comparator #(.width(4), .mode("unsigned")) comparator_1 (
    .a(B[3:0]), .b(4'b0000), .eq(comparator_1_eq));  // open: gt, lt
  Multiplexer #(.select(2)) multiplexer_1 (
    .in0(addition_and_subratction_1_sign), .in1(addition_and_subratction_1_sign), .in2(multiplication_1_f9),
    .in3(division_1_sign), .out(Sign_Flag), .sel(in_1));  // open: en
  Multiplexer #(.select(2), .width(8)) multiplexer_2 (
    .in0(addition_and_subratction_1_result), .in1(addition_and_subratction_1_result),
    .in2(multiplication_1_f1), .in3(multiplexer_3_out), .out(Result), .sel(in_1));  // open: en
  Multiplexer #(.width(8)) multiplexer_3 (
    .in0(division_1_out_4), .out(multiplexer_3_out), .sel(comparator_1_eq));  // open: in1, en
  Comparator #(.width(2)) comparator_2 (.a(in_1), .b(2'b11), .eq(comparator_2_eq));  // open: gt, lt
  Comparator comparator_3 (.a(Result), .b({8{1'b0}}), .eq(Zero_Flag));  // open: gt, lt
  Multiplexer multiplexer_4 (.in1(comparator_1_eq), .out(Div_by_Zero_Flag), .sel(comparator_2_eq));  // open: in0, en

  // Notes on the sheet:
  //   Method of operation
  //   Addition and Subtraction
  //   Multiplication
  //   Division
  //   If Divsion
endmodule
