// Logisim project Multiplication final.circ as structural Verilog: 3 circuits, main circuit halfadder
module halfadder (
  input  in_1,
  input  in_2,
  output sum,
  output carry
);

  xor xor_1 (sum, in_1, in_2);
  and and_1 (carry, in_1, in_2);
endmodule

module fulladder (
  input  in_1,
  input  in_2,
  input  in_3,
  output sum,
  output carry
);

  wire halfadder_1_carry, halfadder_1_sum, halfadder_2_carry;

  halfadder halfadder_1 (.in_1(in_1), .in_2(in_2), .sum(halfadder_1_sum), .carry(halfadder_1_carry));
  halfadder halfadder_2 (.in_1(halfadder_1_sum), .in_2(in_3), .sum(sum), .carry(halfadder_2_carry));
  or or_1 (carry, halfadder_2_carry, halfadder_1_carry);
endmodule

module multiplication (
  input  a0,
  input  a1,
  input  a2,
  input  a3,
  input  a4,
  input  b0,
  input  b1,
  input  b2,
  input  b3,
  input  b4,
  output f1,
  output f2,
  output f3,
  output f4,
  output f5,
  output f6,
  output f7,
  output f8,
  output f9
);

  wire a2b3_out, and_2_out, and_3_out, and_4_out, and_5_out, and_6_out, and_7_out, and_8_out, and_9_out,
       and_10_out, and_11_out, and_12_out, and_13_out, b2a3_out, b3a3_out, fulladder_1_carry,
       fulladder_1_sum, fulladder_2_carry, fulladder_2_sum, fulladder_3_carry, fulladder_3_sum,
       fulladder_4_carry, fulladder_4_sum, fulladder_5_carry, fulladder_5_sum, fulladder_6_carry,
       fulladder_6_sum, fulladder_7_carry, HA_carry, halfadder_1_carry, halfadder_2_carry, halfadder_3_carry;

  and and_1 (f1, a0, b0);
  and and_2 (and_2_out, a1, b0);
  and and_3 (and_3_out, a0, b1);
  and and_4 (and_4_out, a0, b3);
  and and_5 (and_5_out, a3, b1);
  halfadder HA (.in_1(and_2_out), .in_2(and_3_out), .sum(f2), .carry(HA_carry));
  fulladder fulladder_1 (
    .in_1(HA_carry), .in_2(and_6_out), .in_3(and_7_out), .sum(fulladder_1_sum), .carry(fulladder_1_carry));
  and and_6 (and_6_out, b0, a2);
  and and_7 (and_7_out, a1, b1);
  and and_8 (and_8_out, a0, b2);
  and and_9 (and_9_out, b0, a3);
  and and_10 (and_10_out, b1, a2);
  and and_11 (and_11_out, a1, b2);
  halfadder halfadder_1 (.in_1(fulladder_1_sum), .in_2(and_8_out), .sum(f3), .carry(halfadder_1_carry));
  fulladder fulladder_2 (
    .in_1(fulladder_1_carry), .in_2(and_9_out), .in_3(and_10_out), .sum(fulladder_2_sum),
    .carry(fulladder_2_carry));
  halfadder halfadder_2 (.in_1(fulladder_3_sum), .in_2(and_4_out), .sum(f4), .carry(halfadder_2_carry));
  and and_12 (and_12_out, a2, b2);
  and and_13 (and_13_out, a1, b3);
  and a2b3 (a2b3_out, a2, b3);
  and b3a3 (b3a3_out, b3, a3);
  fulladder fulladder_3 (
    .in_1(halfadder_1_carry), .in_2(fulladder_2_sum), .in_3(and_11_out), .sum(fulladder_3_sum),
    .carry(fulladder_3_carry));
  fulladder fulladder_4 (
    .in_1(fulladder_3_carry), .in_2(fulladder_2_carry), .in_3(and_5_out), .sum(fulladder_4_sum),
    .carry(fulladder_4_carry));
  fulladder fulladder_5 (
    .in_1(fulladder_4_sum), .in_2(halfadder_2_carry), .in_3(and_12_out), .sum(fulladder_5_sum),
    .carry(fulladder_5_carry));
  and b2a3 (b2a3_out, a3, b2);
  fulladder fulladder_6 (
    .in_1(fulladder_5_carry), .in_2(fulladder_4_carry), .in_3(b2a3_out), .sum(fulladder_6_sum),
    .carry(fulladder_6_carry));
  halfadder halfadder_3 (.in_1(fulladder_5_sum), .in_2(and_13_out), .sum(f5), .carry(halfadder_3_carry));
  fulladder fulladder_7 (
    .in_1(halfadder_3_carry), .in_2(fulladder_6_sum), .in_3(a2b3_out), .sum(f6), .carry(fulladder_7_carry));
  fulladder fulladder_8 (.in_1(fulladder_7_carry), .in_2(fulladder_6_carry), .in_3(b3a3_out), .sum(f7), .carry(f8));
  xor xor_1 (f9, a4, b4);

  // Notes on the sheet:
  //   b0a0
  //   b0a1
  //   b1a3
  //   b1a0
  //   boa2
  //   b3a0
  //   FA
  //   HA
  //   b1a1
  //   b2a0
  //   boa3
  //   b1a2
  //   b2a1
  //   HA
  //   b2a2
  //   FA
  //   a1b3
  //   FA
  //   FA
  //   FA
  //   HA
  //   FA
  //   FA
  //   FA
  //   SIGN
endmodule
