// Logisim project final.circ as structural Verilog: 6 circuits, main circuit Addition and subratction
module Addition_and_subratction (
  input  [4:0] A,
  input  [4:0] in_2,
  input  [1:0] in_3,
  output [7:0] Result,
  output Sign
);

  wire comparator_1_eq, not_1_out;
  wire [3:0] multiplexer_1_out, multiplexer_2_out, n2_s_complement_1_out_2, n2_s_complement_2_out_2;
  wire [4:0] n2_s_complemet_5_bits_1_out_2, n6bit_6bit_1_out_3;
  wire [5:5] multiplexer_3_out;

  _2_s_complement u_2_s_complement_1 (.in_1(A[3:0]), .out_2(n2_s_complement_1_out_2));
  _2_s_complement u_2_s_complement_2 (.in_1(in_2[3:0]), .out_2(n2_s_complement_2_out_2));
  Comparator #(.width(2), .mode("unsigned")) comparator_1 (.a(in_3), .b(2'b01), .eq(comparator_1_eq));  // open: gt, lt
  Multiplexer #(.width(4)) multiplexer_1 (
    .in0(A[3:0]), .in1(n2_s_complement_1_out_2), .out(multiplexer_1_out), .sel(A[4]));  // open: en
  Multiplexer #(.width(4)) multiplexer_2 (
    .in0(in_2[3:0]), .in1(n2_s_complement_2_out_2), .out(multiplexer_2_out), .sel(multiplexer_3_out[5]));  // open: en
  not not_1 (not_1_out, in_2[4]);
  Multiplexer multiplexer_3 (
    .in0(in_2[4]), .in1(not_1_out), .out(multiplexer_3_out[5]), .sel(comparator_1_eq));  // open: en
  _6bit_6bit u_6bit_6bit_1 (
    .in_1({{2{A[4]}}, multiplexer_1_out}), .in_2({{2{multiplexer_3_out[5]}}, multiplexer_2_out}),
    .out_3(n6bit_6bit_1_out_3), .Sign(Sign));
  _2_s_complemet_5_bits u_2_s_complemet_5_bits_1 (.in_1(n6bit_6bit_1_out_3), .out_2(n2_s_complemet_5_bits_1_out_2));
  Multiplexer #(.width(5)) multiplexer_4 (
    .in0(n6bit_6bit_1_out_3), .in1(n2_s_complemet_5_bits_1_out_2), .out(Result[4:0]), .sel(Sign));  // open: en

  assign Result[7:5] = 3'b000;

  // Notes on the sheet:
  //   B
  //   2's complemet
  //   2's complement
  //   2's complement
endmodule

module _2_s_complement (
  input  [3:0] in_1,
  output [3:0] out_2
);

  wire comparator_1_eq;
  wire [3:0] n1_bit_4_bits_1_out_2, not_1_out;

  Comparator #(.width(4), .mode("unsigned")) comparator_1 (
    .a(in_1), .b(4'b0000), .eq(comparator_1_eq));  // open: gt, lt
  assign not_1_out = ~in_1;  // NOT_Gate not_1, 4 bits wide
  _1_bit_4_bits u_1_bit_4_bits_1 (.in_1(not_1_out), .out_2(n1_bit_4_bits_1_out_2));
  Multiplexer #(.width(4)) multiplexer_1 (
    .in0(n1_bit_4_bits_1_out_2), .in1(in_1), .out(out_2), .sel(comparator_1_eq));  // open: en
endmodule

module _1_bit_4_bits (
  input  [3:0] in_1,
  output [3:0] out_2
);

  wire halfadder_1_p4, halfadder_2_p4, halfadder_3_p4;

  // halfadder halfadder_1: pin names not known; wires that end beside it: in_1[0], 1'b1, out_2[0], halfadder_1_p4
  // halfadder halfadder_2: pin names not known; wires that end beside it: halfadder_1_p4, in_1[1], out_2[1], halfadder_2_p4
  // halfadder halfadder_3: pin names not known; wires that end beside it: halfadder_2_p4, in_1[2], out_2[2], halfadder_3_p4
  // halfadder halfadder_4: pin names not known; wires that end beside it: halfadder_3_p4, in_1[3], out_2[3], 1'b0
endmodule

module _6bit_6bit (
  input  [5:0] in_1,
  input  [5:0] in_2,
  output [4:0] out_3,
  output Sign
);

  wire fulladder_1_p5, fulladder_2_p5, fulladder_3_p5, fulladder_4_p5, halfadder_1_p4;

  // halfadder halfadder_1: pin names not known; wires that end beside it: in_1[0], in_2[0], out_3[0], halfadder_1_p4
  // fulladder fulladder_1: pin names not known; wires that end beside it: in_1[1], in_2[1], halfadder_1_p4, out_3[1], fulladder_1_p5
  // fulladder fulladder_2: pin names not known; wires that end beside it: in_1[2], in_2[2], fulladder_1_p5, out_3[2], fulladder_2_p5
  // fulladder fulladder_3: pin names not known; wires that end beside it: in_1[3], in_2[3], fulladder_2_p5, out_3[3], fulladder_3_p5
  // fulladder fulladder_4: pin names not known; wires that end beside it: in_1[4], in_2[4], fulladder_3_p5, out_3[4], fulladder_4_p5
  // fulladder fulladder_5: pin names not known; wires that end beside it: in_1[5], in_2[5], fulladder_4_p5, Sign, 1'b0
endmodule

module _2_s_complemet_5_bits (
  input  [4:0] in_1,
  output [4:0] out_2
);

  wire comparator_1_eq;
  wire [4:0] n1bit_5_bits_1_out_2, not_1_out;

  Comparator #(.width(5), .mode("unsigned")) comparator_1 (
    .a(in_1), .b({5{1'b0}}), .eq(comparator_1_eq));  // open: gt, lt
  assign not_1_out = ~in_1;  // NOT_Gate not_1, 5 bits wide
  _1bit_5_bits u_1bit_5_bits_1 (.in_1(not_1_out), .out_2(n1bit_5_bits_1_out_2));
  Multiplexer #(.width(5)) multiplexer_1 (
    .in0(n1bit_5_bits_1_out_2), .in1(in_1), .out(out_2), .sel(comparator_1_eq));  // open: en
endmodule

module _1bit_5_bits (
  input  [4:0] in_1,
  output [4:0] out_2
);

  wire halfadder_1_p4, halfadder_2_p4, halfadder_3_p4, halfadder_4_p4;

  // halfadder halfadder_1: pin names not known; wires that end beside it: in_1[0], 1'b1, out_2[0], halfadder_1_p4
  // halfadder halfadder_2: pin names not known; wires that end beside it: halfadder_1_p4, in_1[1], out_2[1], halfadder_2_p4
  // halfadder halfadder_3: pin names not known; wires that end beside it: halfadder_2_p4, in_1[2], out_2[2], halfadder_3_p4, out_2
  // halfadder halfadder_4: pin names not known; wires that end beside it: halfadder_3_p4, in_1[3], out_2[3], halfadder_4_p4
  // halfadder halfadder_5: pin names not known; wires that end beside it: halfadder_4_p4, in_1[4], out_2[4], 1'b0
endmodule
